# Fritzing sketch Circuito (saved by Fritzing 0.7.1b)
breadboards: 1

parts:
  U1 = Arduino Mega
  R1 = Resistor [tolerance=±5% resistance=180 package=THT]
  LED1 = LED - 3mm [color="Red (633nm)" package="3 mm [THT]"]

nets:
  N1: U1.GND, R1.Pin_1
  N2: U1.D13, LED1.cathode
  N3: R1.Pin_0, LED1.anode
